# Fritzing sketch afficheur_moto_smd (saved by Fritzing 1.0.6)
circuit board: 3.61569cm x 3.38787cm
breadboards: 1

parts:
  J1 = female pin header, 6 pins [form="♀ (female)"]
  J2 = female pin header, 9 pins [form="♀ (female)"]
  J3 = female pin header, 1 pin [form="♀ (female)"]
  D16 = Rectifier Diode [package="Melf DO-213 AA [SMD]"]
  D19 = Rectifier Diode [package="Melf DO-213 AA [SMD]"]
  D1 = Rectifier Diode [package="Melf DO-213 AA [SMD]"]
  D5 = Rectifier Diode [package="Melf DO-213 AA [SMD]"]
  D7 = Rectifier Diode [package="Melf DO-213 AA [SMD]"]
  D2 = Rectifier Diode [package="Melf DO-213 AA [SMD]"]
  D6 = Rectifier Diode [package="Melf DO-213 AA [SMD]"]
  D4 = Rectifier Diode [package="Melf DO-213 AA [SMD]"]
  D3 = Rectifier Diode [package="Melf DO-213 AA [SMD]"]
  D12 = Rectifier Diode [package="Melf DO-213 AA [SMD]"]
  D11 = Rectifier Diode [package="Melf DO-213 AA [SMD]"]
  D9 = Rectifier Diode [package="Melf DO-213 AA [SMD]"]
  D8 = Rectifier Diode [package="Melf DO-213 AA [SMD]"]
  D15 = Rectifier Diode [package="Melf DO-213 AA [SMD]"]
  D13 = Rectifier Diode [package="Melf DO-213 AA [SMD]"]
  D14 = Rectifier Diode [package="Melf DO-213 AA [SMD]"]
  D17 = Rectifier Diode [package="Melf DO-213 AA [SMD]"]
  D21 = Rectifier Diode [package="Melf DO-213 AA [SMD]"]
  D20 = Rectifier Diode [package="Melf DO-213 AA [SMD]"]
  D18 = Rectifier Diode [package="Melf DO-213 AA [SMD]"]
  D22 = Rectifier Diode [package="Melf DO-213 AA [SMD]"]
  R1 = Resistor [tolerance=±5% resistance=680 power=0.25W package="1206 [SMD]"]
  R2 = Resistor [tolerance=±5% resistance=680 power=0.25W package="1206 [SMD]"]
  R3 = Resistor [tolerance=±5% resistance=680 power=0.25W package="1206 [SMD]"]
  R4 = Resistor [tolerance=±5% resistance=680 power=0.25W package="1206 [SMD]"]
  R5 = Resistor [tolerance=±5% resistance=680 power=0.25W package="1206 [SMD]"]
  R6 = Resistor [tolerance=±5% resistance=680 power=0.25W package="1206 [SMD]"]
  R7 = Resistor [tolerance=±5% resistance=680 power=0.25W package="1206 [SMD]"]
  R8 = Resistor [tolerance=±5% resistance=680 power=0.25W package="1206 [SMD]"]
  D10 = Rectifier Diode [package="Melf DO-213 AA [SMD]"]
  D23 = Rectifier Diode [package="Melf DO-213 AA [SMD]"]
  D24 = Rectifier Diode [package="Melf DO-213 AA [SMD]"]
  D25 = Rectifier Diode [package="Melf DO-213 AA [SMD]"]
  D26 = Rectifier Diode [package="Melf DO-213 AA [SMD]"]
  D27 = Rectifier Diode [package="Melf DO-213 AA [SMD]"]
  D28 = Rectifier Diode [package="Melf DO-213 AA [SMD]"]

nets:
  N1: J1.pin1, D1.cathode, D2.cathode
  N2: J1.pin2, D5.cathode, D7.cathode, D6.cathode, D4.cathode, D3.cathode
  N3: J1.pin3, D12.cathode, D11.cathode, D9.cathode, D8.cathode, D10.cathode
  N4: J1.pin4, D16.cathode, D15.cathode, D13.cathode, D14.cathode
  N5: J1.pin5, D19.cathode, D17.cathode, D21.cathode, D20.cathode, D18.cathode
  N6: J1.pin6, D22.cathode, D23.cathode, D24.cathode, D25.cathode, D26.cathode, D27.cathode, D28.cathode
  N7: J2.pin1, R1.Pin_1
  N8: J2.pin2, R2.Pin_1
  N9: J2.pin3, R3.Pin_1
  N10: J2.pin4, R4.Pin_1
  N11: J2.pin5, R5.Pin_1
  N12: J2.pin6, R6.Pin_1
  N13: J2.pin7, R7.Pin_1
  N14: J2.pin8, R8.Pin_1
  N15: J2.pin9, J3.pin1
  N16: D16.anode, D2.anode, D9.anode, D21.anode, R3.Pin_0, D25.anode
  N17: D19.anode, D7.anode, R4.Pin_0, D10.anode, D26.anode
  N18: D1.anode, D4.anode, D11.anode, D13.anode, R2.Pin_0, D24.anode
  N19: D5.anode, D8.anode, D14.anode, D20.anode, R7.Pin_0
  N20: D6.anode, R5.Pin_0, D27.anode
  N21: D3.anode, D12.anode, D17.anode, R1.Pin_0, D23.anode
  N22: D15.anode, D18.anode, R6.Pin_0, D28.anode
  N23: D22.anode, R8.Pin_0

notes:
  12V
  1
  a
  D1-D22 : 1N4001
  R1-R8 : 680Ω 1/4W
  1 2  3 4  5 N
  a  b  c d  e  f  g h 12v
  Afficheur 7 segments à anode commune
  Prévu pour 5 rapports + N en 12v
  N
